# Fritzing sketch pilight lamp Sketch (saved by Fritzing 0.9.1b)
circuit board: 3.1825cm x 1.96065cm
breadboards: 1

parts:
  R1 = Resistor [tolerance=±5% resistance=470 package=THT]
  R2 = Resistor [tolerance=±5% resistance=1.5k package=THT]
  Q1 = NPN-Transistor [package="TO92 [THT]"]
  Raspberry_Pi1 = Raspberry Pi B+
  LED1 = LED - 3mm [color="Red (633nm)" package="3 mm [THT]"]
  J5 = Screw terminal - 2 pins [package=THT]
  J9 = Screw terminal - 2 pins [package=THT]
  J8 = Screw terminal - 2 pins [package=THT]
  J7 = screw terminal, 2 pins

nets:
  N1: R1.Pin_0, R2.Pin_0, Raspberry_Pi1.GPIO17, J7.pin1
  N2: R1.Pin_1, LED1.cathode
  N3: R2.Pin_1, Q1.B
  GND: Q1.E, Raspberry_Pi1.GND, LED1.anode, J9.pin1
  N4: Q1.C, J5.pin2
  5V: Raspberry_Pi1.5V, J8.pin1
